# Fritzing sketch AXDL334_Sketch (saved by Fritzing 0.9.1b)
breadboards: 1

parts:
  パーツ1 = Arduino Uno (Rev3)
  IC1 = IC, DIP package, 8 pins [chip_label=IC]

nets:
  N1: パーツ1.A0, IC1.pin6
  N2: パーツ1.A1, IC1.pin7
  N3: パーツ1.A2, IC1.pin8
  N4: パーツ1.3V3, IC1.pin1
  N5: パーツ1.GND, IC1.pin3
